# Fritzing sketch Untitled Sketch 2 (saved by Fritzing 0.9.2b)
breadboards: 1

parts:
  M2 = NEO-6M GPS Module [part_number=GY-GPS6MV2]
  U1 = SD_CARD_SOCKET [package=sdcard_4uconn]
  Part1 = Arduino Uno (Rev3) - ICSP
  Part2 = Arduino GSM Shield

nets:
  GND: M2.GND, Part1.GND, Part2.AGND
  N1: M2.Tx, Part1.D5_PWM
  N2: M2.Rx, Part1.D6_PWM
  5V: M2.Vcc, U1.DAT0, Part1.5V, Part2.5V
  N3: U1.DAT1, Part1.D4
  N4: U1.DAT2, Part1.D12/MISO
  N5: U1.CD, Part1.D11_PWM/MOSI
  N6: U1.WP, Part1.D13/SCK
  N7: Part1.D8, Part2.RST_MDM/D7
  N8: Part1.D7, Part2.D8

custom parts:
  NEO-6M GPS Module: GY-GPS6MV2 NEO-6M GPS Module Module based on U-blox NEO-6M GPS engine, incorporating regulator for 3.3-5V DC input, MS621FE-compatible rechargeable battery for backup and EEPROM for storing configuration settings. Links: NEO-6 series product information page NEO-6 Datasheet
